# Fritzing sketch batteryboard (saved by Fritzing 0.9.2b)
circuit board: 2.08618cm x 3.23018cm
breadboards: 1

parts:
  PWR = female pin header, 2 pins [form="♀ (female)"]
  SER = female pin header, 3 pins [form="♀ (female)"]
  AIN = female pin header, 6 pins [form="♀ (female)"]
  VOUT = female pin header, 2 pins [form="♀ (female)"]
  PWM = female pin header, 5 pins [form="♀ (female)"]
  BATT = Header 2 [package=jst-2-pth]
  EXT = Screw terminal - 2 pins [package=THT]
  sw1 = DIP SWITCH [package=dipswitch-02]

nets:
  N1: PWR.pin1, sw1.1, sw1.2
  N2: PWR.pin2, SER.pin1, AIN.pin1, VOUT.pin2, PWM.pin1, BATT.1, EXT.pin1
  N3: BATT.2, sw1.3
  N4: EXT.pin2, sw1.4

notes:
  nSST lipob 150709001
  ©2015 Kyra Zimmer
  nSSt.nonchip.de
