# Fritzing sketch cpuboard (saved by Fritzing 0.9.2b)
circuit board: 2.36982cm x 2.10246cm
breadboards: 1

parts:
  Att84 = Attiny 44/84 [package="DIP (Dual Inline) [THT]"]
  J1 = female pin header, 3 pins [form="♀ (female)"]
  J4 = female pin header, 7 pins [form="♀ (female)"]
  J5 = female pin header, 7 pins [form="♀ (female)"]

nets:
  N1: Att84.VCC, J1.pin1, J4.pin1
  N2: Att84.PB0, J4.pin2
  N3: Att84.PB1, J4.pin3
  N4: Att84.PB3, J1.pin2, J4.pin4
  N5: Att84.PB2, J4.pin5
  N6: Att84.PA7, J4.pin6
  N7: Att84.PA6, J4.pin7
  N8: Att84.PA5, J5.pin7
  N9: Att84.PA4, J5.pin6
  N10: Att84.PA3, J5.pin5
  N11: Att84.PA2, J5.pin4
  N12: Att84.PA1, J5.pin3
  N13: Att84.PA0, J5.pin2
  N14: Att84.GND, J1.pin3, J5.pin1

notes:
  nSST.nonchip.de/mb/1
