# Fritzing sketch hackboard (saved by Fritzing 0.9.2b)
circuit board: 2.36982cm x 2.10246cm
breadboards: 1

parts:
  J1 = female pin header, 3 pins [form="♀ (female)"]
  J4 = female pin header, 7 pins [form="♀ (female)"]
  J5 = female pin header, 7 pins [form="♀ (female)"]
  J6 = double row female pin header, 14 pins [form="♀ (female)"]
  J7 = double row female pin header, 14 pins [form="♀ (female)"]  # not connected
  J8 = double row female pin header, 14 pins [form="♀ (female)"]
  J9 = female pin header, 6 pins [form="♀ (female)"]  # not connected

nets:
  N1: J1.pin1, J4.pin1, J8.pin1
  N2: J1.pin3, J5.pin1, J6.pin14
  N3: J4.pin2, J8.pin2
  N4: J4.pin3, J8.pin3
  N5: J4.pin4, J8.pin4
  N6: J4.pin5, J8.pin5
  N7: J4.pin6, J8.pin6
  N8: J4.pin7, J8.pin7
  N9: J5.pin2, J6.pin13
  N10: J5.pin3, J6.pin12
  N11: J5.pin4, J6.pin11
  N12: J5.pin5, J6.pin10
  N13: J5.pin6, J6.pin9
  N14: J5.pin7, J6.pin8

notes:
  hackSST
