# Fritzing sketch mainboard (saved by Fritzing 0.9.2b)
circuit board: 2.08618cm x 3.23018cm
breadboards: 1

parts:
  U2 = Voltage Regulator - 5V [package="TO220 [THT]"]
  PWR = female pin header, 2 pins [form="♀ (female)"]
  RST = Pushbutton [package="[THT]"]
  Att48 = Attiny 44/84 [package="DIP (Dual Inline) [THT]"]
  SER = female pin header, 3 pins [form="♀ (female)"]
  PWM = female pin header, 5 pins [form="♀ (female)"]
  AIN = female pin header, 6 pins [form="♀ (female)"]
  VOUT = female pin header, 2 pins [form="♀ (female)"]

nets:
  N1: U2.input_voltage, PWR.pin1
  GND: U2.GND, PWR.pin2, RST.Pin_3, RST.Pin_4, Att48.GND, SER.pin1, PWM.pin1, AIN.pin1, VOUT.pin2
  N2: U2.output_voltage, Att48.VCC, VOUT.pin1
  N3: RST.Pin_1, RST.Pin_2, Att48.PB3
  N4: Att48.PB0, SER.pin2
  N5: Att48.PB1, SER.pin3
  N6: Att48.PB2, PWM.pin2
  N7: Att48.PA7, PWM.pin3
  N8: Att48.PA6, PWM.pin4
  N9: Att48.PA5, PWM.pin5
  N10: Att48.PA4, AIN.pin6
  N11: Att48.PA3, AIN.pin5
  N12: Att48.PA2, AIN.pin4
  N13: Att48.PA1, AIN.pin3
  N14: Att48.PA0, AIN.pin2

notes:
  nSST mb 150709001
  ©2015 Kyra Zimmer
  nSSt.nonchip.de
