# Fritzing sketch motorboard2 (saved by Fritzing 0.9.2b)
circuit board: 2.08618cm x 3.23018cm
breadboards: 1

parts:
  PWR = female pin header, 2 pins [form="♀ (female)"]
  SER = female pin header, 3 pins [form="♀ (female)"]
  PWM = female pin header, 5 pins [form="♀ (female)"]
  AIN = female pin header, 6 pins [form="♀ (female)"]
  VOUT = female pin header, 2 pins [form="♀ (female)"]
  Q1 = NPN-Transistor [package="TO92 [THT]"]
  Q2 = NPN-Transistor [package="TO92 [THT]"]
  SW1 = DIP SWITCH [package=dipswitch-02]
  C3 = Ceramic Capacitor [capacitance=100nF package="100 mil [THT, multilayer]"]
  C4 = Ceramic Capacitor [capacitance=100nF package="100 mil [THT, multilayer]"]
  J3 = Screw terminal - 2 pins [package=THT]
  J4 = Screw terminal - 2 pins [package=THT]
  R3 = Resistor [tolerance=±5% resistance=1k package="0805 [SMD]"]
  R4 = Resistor [tolerance=±5% resistance=1k package="0805 [SMD]"]
  D1 = Rectifier Diode [package="Melf DO-213 AA [SMD]"]
  D2 = Rectifier Diode [package="Melf DO-213 AA [SMD]"]

nets:
  GND: PWR.pin2, SER.pin1, PWM.pin1, AIN.pin1, VOUT.pin2, Q1.C, Q2.C
  N1: PWM.pin4, SW1.1
  N2: PWM.pin5, SW1.2
  N3: VOUT.pin1, C3.0, C4.0, J3.pin1, J4.pin1, D1.cathode, D2.cathode
  N4: Q1.E, C3.1, J3.pin2, D1.anode
  N5: Q1.B, R3.Pin_0
  N6: Q2.E, C4.1, J4.pin2, D2.anode
  N7: Q2.B, R4.Pin_0
  N8: SW1.3, R4.Pin_1
  N9: SW1.4, R3.Pin_1

notes:
  nSST mdb2 150709001
  ©2015 Kyra Zimmer
  nSSt.nonchip.de
