# Fritzing sketch motorboardAdv (saved by Fritzing 0.9.2b)
circuit board: 2.08618cm x 3.23018cm
breadboards: 1

parts:
  PWR = female pin header, 2 pins [form="♀ (female)"]
  SER = female pin header, 3 pins [form="♀ (female)"]
  PWM = female pin header, 5 pins [form="♀ (female)"]
  AIN = female pin header, 6 pins [form="♀ (female)"]
  VOUT = female pin header, 2 pins [form="♀ (female)"]
  Q1 = NPN-Transistor [package="TO92 [THT]"]
  Q2 = NPN-Transistor [package="TO92 [THT]"]
  C3 = Ceramic Capacitor [capacitance=100nF package="100 mil [THT, multilayer]"]
  C4 = Ceramic Capacitor [capacitance=100nF package="100 mil [THT, multilayer]"]
  J3 = Screw terminal - 2 pins [package=THT]
  J4 = Screw terminal - 2 pins [package=THT]
  R3 = Resistor [tolerance=±5% resistance=1k package="0805 [SMD]"]
  D1 = Rectifier Diode [package="Melf DO-213 AA [SMD]"]
  D2 = Rectifier Diode [package="Melf DO-213 AA [SMD]"]
  Pad2 = Pad [width=11.2641501844203 height=0.825142049943654 connect=center]
  R4 = Resistor [tolerance=±5% resistance=1k package="0805 [SMD]"]
  Pad1 = Pad [width=11.2625143647182 height=0.825142049943654 connect=center]
  Pad4 = Pad [width=1.19384427949913 height=1.75926953997147 connect=center]
  Pad5 = Pad [width=1.19384427949913 height=1.75926953997147 connect=center]
  Pad6 = Pad [width=1.19384427949913 height=1.75926953997147 connect=center]
  Pad7 = Pad [width=1.19384427949913 height=1.75926953997147 connect=center]
  Pad3 = Pad [width=1.19384427949913 height=1.75926953997147 connect=center]
  Pad8 = Pad [width=1.19384427949913 height=1.75926953997147 connect=center]
  Pad9 = Pad [width=1.19384427949913 height=1.75926953997147 connect=center]
  Pad10 = Pad [width=1.19384427949913 height=1.75926953997147 connect=center]

nets:
  GND: PWR.pin2, SER.pin1, PWM.pin1, AIN.pin1, VOUT.pin2, Q1.C, Q2.C
  N1: PWM.pin2, Pad4.pad, Pad3.pad
  N2: PWM.pin3, Pad5.pad, Pad8.pad
  N3: PWM.pin4, Pad6.pad, Pad9.pad
  N4: PWM.pin5, Pad7.pad, Pad10.pad
  N5: VOUT.pin1, C3.0, C4.0, J3.pin1, J4.pin1, D1.cathode, D2.cathode
  N6: Q1.E, C3.1, J3.pin2, D1.anode
  N7: Q1.B, R3.Pin_0
  N8: Q2.E, C4.1, J4.pin2, D2.anode
  N9: Q2.B, R4.Pin_1
  N10: R3.Pin_1, Pad2.pad
  N11: R4.Pin_0, Pad1.pad

notes:
  nSST a2mb 150709001
  ©2015 Kyra Zimmer
  nSSt.nonchip.de
