# Fritzing sketch powerboard (saved by Fritzing 0.9.2b)
circuit board: 2.36982cm x 2.10246cm
breadboards: 1

parts:
  J1 = female pin header, 3 pins [form="♀ (female)"]
  J4 = female pin header, 7 pins [form="♀ (female)"]
  J5 = female pin header, 7 pins [form="♀ (female)"]
  U1 = Voltage Regulator - 5V [package="TO220 [THT]"]
  J6 = female pin header, 2 pins [form="♀ (female)"]
  J7 = Screw terminal - 2 pins [package=THT]

nets:
  N1: J1.pin1, J4.pin1, U1.output_voltage
  N2: J1.pin3, J5.pin1, U1.GND, J6.pin2, J7.pin2
  N3: U1.input_voltage, J6.pin1, J7.pin1

notes:
  nSST.nonchip.de/pb/1
